# Fritzing sketch 原理图 (saved by Fritzing 0.9.5d)

parts:
  Raspberry_Pi_1 = Raspberry Pi 3 [part_number=RPI-3-V1.2]
  SG1 = Buzzer 12mm [package=buzzer-12mm]
  LED1 = LEDs [package=led10mm]
  R1 = Resistor [tolerance=±5% resistance=220 package="0603 [SMD]"]
  U2 = LCD-16X2 [package=lcd-8x2-kit]
  MQ-3 = MQ-3 breakout
  ADC1 = MCP3008 [package=dil16]
  2_2k_Ω = Resistor [tolerance=±5% resistance=220 package=THT]

nets:
  N1: Raspberry_Pi_1.GIPO10, ADC1.Din
  N2: Raspberry_Pi_1.GIPO9, ADC1.Dout
  N3: Raspberry_Pi_1.GIPO11, ADC1.CLK
  N4: Raspberry_Pi_1.GIPO21, SG1.1
  N5: Raspberry_Pi_1.GIPO20, R1.Pin_1
  N6: Raspberry_Pi_1.GIPO12, U2.E
  N7: Raspberry_Pi_1.GIPO7, U2.RS
  N8: Raspberry_Pi_1.GIPO8, ADC1.CS/SHDN
  N9: Raspberry_Pi_1.GIPO25, U2.DB4
  N10: Raspberry_Pi_1.GIPO24, U2.DB5
  N11: Raspberry_Pi_1.GIPO23, U2.DB6
  GND: Raspberry_Pi_1.GND, SG1.2, LED1.C, U2.VSS, U2.VO, U2.R_W, U2.K, MQ-3.GND, ADC1.DGND, ADC1.AGND
  N12: Raspberry_Pi_1.GIPO18, U2.DB7
  VDD: Raspberry_Pi_1.5V, U2.VDD, ADC1.VREF, ADC1.VDD, 2_2k_Ω.Pin_1
  N13: LED1.A, R1.Pin_0
  N14: U2.A, 2_2k_Ω.Pin_0
  N15: MQ-3.AO, ADC1.CH0

custom parts:
  MQ-3 breakout: Alcohol sensor is capable of detecting alcohol (ethanol) particles on itself and gives the information in digital form back to us to manipulate with it. SKU:101251 • Voltage: 5V DC • Power: max 750mW • Measurement range: 0.04-4mg/L
